# Fritzing sketch NodeMcuFingerprint (saved by Fritzing 0.9.3b)
breadboards: 1

parts:
  U1 = NodeMCU V1.0
  Composant1 = sensor_biometrico
  Q1 = TRANSISTOR_NPN [part_number=2N2222 package=to-92]
  VCC1 = 4 x AAA Battery Mount
  R1 = Resistor [tolerance=±5% resistance=1k package="0402 [SMD]"]
  R2 = Resistor [tolerance=±5% resistance=47 package="0402 [SMD]"]
  R3 = Resistor [tolerance=±5% resistance=10 package="0402 [SMD]"]
  R4 = Resistor [tolerance=±5% resistance=68 package="0402 [SMD]"]
  R5 = Resistor [tolerance=±5% resistance=33 package="0402 [SMD]"]
  LED1 = LED - 3mm [color="Green (570nm)" package="3 mm [THT]"]

nets:
  N1: U1.D1, R1.Pin_1
  N2: U1.GND, Q1.E, VCC1.-, LED1.cathode
  N3: U1.D5, Composant1.TX
  N4: U1.D6, Composant1.RX
  N5: U1.D7, R2.Pin_1
  N6: U1.Vin, VCC1.+, R3.Pin_0
  N7: Composant1.VCC, R3.Pin_1, R4.Pin_1
  N8: Composant1.GND, Q1.C, R5.Pin_1
  N9: Q1.B, R1.Pin_0
  N10: R2.Pin_0, LED1.anode
  N11: R4.Pin_0, R5.Pin_0

custom parts:
  NodeMCU V1.0: ESP9266 based NodeMCU
  sensor_biometrico: Adafruit Optical Fingerprint Sensor
