# Fritzing sketch photo_interrupter (saved by Fritzing 0.9.3b)
breadboards: 1

parts:
  Part2 = Photo Interrupter Module OS 1990-2335
  Composant1 = Arduino Uno (Rev3)
  R1 = Resistor [tolerance=±5% resistance=220 package=THT]
  R2 = Resistor [tolerance=±5% resistance=4.7k package=THT]

nets:
  N1: Part2.S, Composant1.D8, R2.Pin_1
  N2: Part2.Vin, R1.Pin_1
  N3: Part2.Ground, Composant1.GND
  N4: Composant1.5V, R1.Pin_0, R2.Pin_0

custom parts:
  Photo Interrupter Module OS 1990-2335: Photo Interrupter Module scavenged from HP printer
