# Fritzing sketch Schema (saved by Fritzing 0.9.3b)
breadboards: 1

parts:
  R1 = Rotary Potentiometer (Large) [maximum_resistance=100kΩ package=THT]
  S1 = Square Pushbutton
  LED1 = smd LED [color="Green (565nm)" package="1206 [SMD]"]
  WeMos_D1_Mini1 = WeMos D1 Mini
  R2 = Resistor [tolerance=±5% resistance=10k package="1206 [SMD]"]
  S2 = Toggle Switch [package=THT]
  U1 = LIPO-1000mAh [package=lipo-1000]

nets:
  N1: R1.leg1, S1.leg0, WeMos_D1_Mini1.3V3
  N2: R1.wiper, WeMos_D1_Mini1.A0
  N3: R1.leg2, LED1.cathode, WeMos_D1_Mini1.G, R2.Pin_0, S2.COM
  N4: S1.leg1, WeMos_D1_Mini1.D2, R2.Pin_1
  N5: LED1.anode, WeMos_D1_Mini1.D1
  N6: WeMos_D1_Mini1.5V, U1.+
  N7: S2.L1, U1.-
