# Fritzing sketch WebServer-Mp3-player (saved by Fritzing 0.9.3b)
breadboards: 1

parts:
  U2 = NodeMCU V1.0
  Q1 = npn-Powertransistor [part_number="TIP122 BCE" package="TO220 [THT]"]
  R1 = Resistor [tolerance=±5% resistance=2.2k package="0805 [SMD]"]
  SPKR1 = Loudspeaker
  C1 = Electrolytic Capacitor [capacitance=0.22mF package="200 mil [THT, electrolytic]"]
  VCC1 = Battery block 9V

nets:
  N1: U2.3V3, SPKR1.pin2, C1.+
  N2: U2.GND, Q1.emitter, C1.-, VCC1.-
  N3: U2.RX, R1.Pin_1
  N4: U2.Vin, VCC1.+
  N5: Q1.base, R1.Pin_0
  N6: Q1.collector, SPKR1.pin1

custom parts:
  NodeMCU V1.0: ESP9266 based NodeMCU
