# Fritzing sketch AnalogMultiplex (saved by Fritzing 0.9.3b)
breadboards: 2

parts:
  U1 = 74HC595 [package="DIP16 [THT]"]
  WeMos_D1_Mini1 = WeMos D1 Mini
  R1 = Resistor [tolerance=±5% resistance=100 package="0603 [SMD]"]
  R2 = Resistor [tolerance=±5% resistance=100 package="0603 [SMD]"]
  R3 = Resistor [tolerance=±5% resistance=100 package="0603 [SMD]"]
  R4 = Resistor [tolerance=±5% resistance=100 package="0603 [SMD]"]
  LED1 = LED - 3mm [color="Yellow (595nm)" package="3 mm [THT]"]
  LED2 = LED - 3mm [color="Yellow (595nm)" package="3 mm [THT]"]
  LED3 = LED - 3mm [color="Yellow (595nm)" package="3 mm [THT]"]
  LED4 = LED - 3mm [color="Yellow (595nm)" package="3 mm [THT]"]
  IC1 = 4060 [part_number=CD4051B package="DIP16 [THT]"]
  S1 = Momentary Switch [package=ksa_sealed_tac_switch]
  S2 = Momentary Switch [package=ksa_sealed_tac_switch]
  U2 = POT [package=alps_pot]
  SW1 = DIP SWITCH [package=dipswitch-02]
  R5 = Resistor [tolerance=±5% resistance=10k package="0603 [SMD]"]
  R6 = Resistor [tolerance=±5% resistance=10k package="0603 [SMD]"]
  R7 = Resistor [tolerance=±5% resistance=10k package="0603 [SMD]"]
  R8 = Resistor [tolerance=±5% resistance=10k package="0603 [SMD]"]

nets:
  N1: U1.Q1, R2.Pin_0
  N2: U1.Q2, R3.Pin_0
  N3: U1.Q3, R4.Pin_0
  GND: U1.GND, U1.OE, LED1.cathode, LED2.cathode, LED3.cathode, LED4.cathode, IC1.Q6, IC1.Q3, IC1.GND, R5.Pin_0, R6.Pin_0, R7.Pin_0, R8.Pin_0
  VCC: U1.MR, U1.VCC, WeMos_D1_Mini1.3V3, IC1.VDD, S1.1, S2.1, U2.E, U2.A
  N4: U1.SH_CP, WeMos_D1_Mini1.D8
  N5: U1.ST_CP, WeMos_D1_Mini1.D7
  N6: U1.DS, WeMos_D1_Mini1.D6
  N7: U1.Q0, R1.Pin_0
  N8: WeMos_D1_Mini1.D1, IC1.REXT
  N9: WeMos_D1_Mini1.D2, IC1.CEXT
  N10: R1.Pin_1, LED1.anode
  N11: R2.Pin_1, LED2.anode
  N12: R3.Pin_1, LED3.anode
  N13: R4.Pin_1, LED4.anode
  N14: IC1.Q11, U2.S
  N15: IC1.MR, SW1.2
  N16: IC1.Q8, S1.4
  N17: IC1.Q7, S2.4
  N18: IC1.Q9, SW1.1
  N19: S1.3, R5.Pin_1
  N20: S2.3, R6.Pin_1
