# Fritzing sketch NeoPixel-Potentiometer (saved by Fritzing 0.9.3b)
breadboards: 1

parts:
  WeMos_D1_Mini1 = WeMos D1 Mini
  U1 = WS2812 RGB LED strip
  VCC1 = Battery block 9V
  U2 = POT [package=pot_mammoth]
  U3 = POT [package=pot_mammoth]
  U4 = POT [package=pot_mammoth]
  D1 = Diode [package=diode-hv]
  D2 = Diode [package=diode-hv]
  D3 = Diode [package=diode-hv]
  R1 = Resistor [tolerance=±5% resistance=10k package="0805 [SMD]"]

nets:
  3V3: WeMos_D1_Mini1.3V3, U1.VCC
  N1: WeMos_D1_Mini1.5V, VCC1.+
  N2: WeMos_D1_Mini1.A0, D1.C, D2.C, D3.C, R1.Pin_0
  N3: WeMos_D1_Mini1.D1, U2.S
  N4: WeMos_D1_Mini1.D2, U3.S
  N5: WeMos_D1_Mini1.D3, U4.S
  N6: WeMos_D1_Mini1.D6, U1.DIN
  N7: WeMos_D1_Mini1.G, VCC1.-
  N8: U1.GND, U2.E, U3.E, U4.E, R1.Pin_1
  N9: U2.A, D1.A
  N10: U3.A, D2.A
  N11: U4.A, D3.A

custom parts:
  WS2812 RGB LED strip: WS2812 strip
